# Fritzing sketch Compass-PCB (saved by Fritzing 0.9.3b)
circuit board: 8.2cm x 8.2cm
breadboards: 1

parts:
  U1 = ATTINY45 [package=so]
  U2 = 74HC595 SMD [package="SO16 [SMD]"]
  LED1 = LEDs [package=fkit-led-1206]
  LED2 = LEDs [package=fkit-led-1206]
  LED3 = LEDs [package=fkit-led-1206]
  LED4 = LEDs [package=fkit-led-1206]
  LED5 = LEDs [package=fkit-led-1206]
  LED6 = LEDs [package=fkit-led-1206]
  LED7 = LEDs [package=fkit-led-1206]
  LED8 = LEDs [package=fkit-led-1206]
  C1 = Capacitor Polarized [package=eia3216]
  J1 = female pin header, 5 pins [form="♀ (female)"]
  J2 = female alternating pin header, 6 pins [form="♀ (female)"]
  BAT1 = Battery Holders [package=battcon_20mm_4legs]
  R5 = Resistor [tolerance=±5% resistance=220 package="1206 [SMD]"]
  R6 = Resistor [tolerance=±5% resistance=220 package="1206 [SMD]"]
  R3 = Resistor [tolerance=±5% resistance=220 package="1206 [SMD]"]
  R1 = Resistor [tolerance=±5% resistance=220 package="1206 [SMD]"]
  R8 = Resistor [tolerance=±5% resistance=220 package="1206 [SMD]"]
  R7 = Resistor [tolerance=±5% resistance=220 package="1206 [SMD]"]
  R4 = Resistor [tolerance=±5% resistance=220 package="1206 [SMD]"]
  U3 = SPDT Slide Switch [package=ayz0202]
  R2 = Resistor [tolerance=±5% resistance=220 package="1206 [SMD]"]

nets:
  N1: U1.PB5(NRES), J2.pin4
  N2: U1.PB3(ADC3), U2.DS
  N3: U1.PB4(ADC2), U2.SH_CP
  GND: U1.GND, U2.GND, U2.OE, LED1.C, LED2.C, LED3.C, LED4.C, LED5.A, LED6.A, LED7.A, LED8.A, C1.-, J1.pin2, J2.pin6, BAT1.-
  N4: U1.PB0(MOSI), J1.pin4, J2.pin1
  N5: U1.PB1(MISO), U2.ST_CP, J2.pin2
  N6: U1.PB2(SCK_ADC1), J1.pin3, J2.pin3
  VCC: U1.VCC, U2.MR, U2.VCC, C1.+, J1.pin1, J2.pin5, U3.2
  N7: U2.Q1, R2.Pin_0
  N8: U2.Q2, R3.Pin_0
  N9: U2.Q3, R4.Pin_0
  N10: U2.Q4, R5.Pin_1
  N11: U2.Q5, R6.Pin_1
  N12: U2.Q6, R7.Pin_1
  N13: U2.Q7, R8.Pin_1
  N14: U2.Q0, R1.Pin_0
  N15: LED1.A, R2.Pin_1
  N16: LED2.A, R1.Pin_1
  N17: LED3.A, R8.Pin_0
  N18: LED4.A, R7.Pin_0
  N19: LED5.C, R6.Pin_0
  N20: LED6.C, R5.Pin_0
  N21: LED7.C, R4.Pin_1
  N22: LED8.C, R3.Pin_1
  N23: BAT1.+, U3.3

notes:
  Skunks Misery 1.0
  05/31 - 06/02 2019
  GRD
  VCC
  RES
  SCK
  MISO
  MOSI
